// Logisim project 1.circ as structural Verilog: 1 circuit, main circuit main
module main (
  input  A,
  input  B,
  input  C,
  input  D,
  input  D_2,
  input  C_2,
  input  B_2,
  input  A_2
);

  wire _0_out, _1_out, _2_out, _3_out, _4_out, _5_out, _6_out, _7_out, _8_out, _14_out, _017_out, _17_out,
       _23_out, _35_out, _56_out, _147_out, _1237_out, _134578_out, and_1_out, and_2_out, and_3_out,
       and_4_out, and_5_out, and_6_out, not_1_out, not_2_out, not_3_out, not_4_out, not_5_out, not_6_out,
       not_7_out, not_8_out, or_1_out;

  not not_1 (not_1_out, A);
  not not_2 (not_2_out, B);
  not not_3 (not_3_out, C);
  not not_4 (not_4_out, D);
  not not_5 (not_5_out, D_2);
  not not_6 (not_6_out, C_2);
  not not_7 (not_7_out, B_2);
  not not_8 (not_8_out, A_2);
  or _0 (_0_out, D_2, C_2, B_2, A_2);
  and and_1 (and_1_out, not_2_out, not_3_out);
  and and_2 (and_2_out, B, C);
  and and_3 (and_3_out, and_1_out, not_4_out);
  and and_4 (and_4_out, and_2_out, D);
  or _1 (_1_out, not_5_out, C_2, B_2, A_2);
  or _2 (_2_out, D_2, not_6_out, B_2, A_2);
  or or_1 (or_1_out, and_3_out, and_4_out);
  and and_5 (and_5_out, and_3_out, not_1_out);
  or _3 (_3_out, not_5_out, not_6_out, B_2, A_2);
  and _23 (_23_out, _2_out, _3_out);
  and and_6 (and_6_out, not_1_out, or_1_out);
  or _4 (_4_out, D_2, C_2, not_7_out, A_2);
  and _17 (_17_out, _1_out, _7_out);
  _7_Segment_Display u_7_segment_display_1 (
    .f(and_5_out), .a(and_6_out), .b(and_6_out), .e(and_5_out), .d(and_5_out), .c(and_6_out));  // open: g, dp
  or _5 (_5_out, not_5_out, C_2, not_7_out, A_2);
  and _35 (_35_out, _3_out, _5_out);
  or _6 (_6_out, D_2, not_6_out, not_7_out, A_2);
  or _7 (_7_out, not_5_out, not_6_out, not_7_out, A_2);
  and _14 (_14_out, _4_out, _1_out);
  and _56 (_56_out, _5_out, _6_out);
  and _147 (_147_out, _14_out, _7_out);
  or _8 (_8_out, not_5_out, C_2, B_2, not_8_out);
  and _134578 (_134578_out, _147_out, _8_out, _35_out);
  and _1237 (_1237_out, _17_out, _23_out);
  _7_Segment_Display u_7_segment_display_2 (
    .g(_017_out), .f(_1237_out), .a(_14_out), .b(_56_out), .e(_134578_out), .d(_147_out), .c(_2_out));  // open: dp
  and _017 (_017_out, _17_out, _0_out);
endmodule
